// Digital circuit CPU.dig as structural Verilog
module CPU (
  input  I0,
  input  I1,
  input  I2,
  input  I3,
  input  I4,
  input  I5,
  input  I6,
  input  I7
);

  wire acumulator_1_s0, acumulator_1_s1, acumulator_1_s2, acumulator_1_s3, acumulator_1_s4, acumulator_1_s5,
       acumulator_1_s6, acumulator_1_s7, Clk, Clr, controller_1_hlt, Cp, Ea, Ep, Eu,
       instruction_register_1_c0, instruction_register_1_c1, instruction_register_1_c2,
       instruction_register_1_c3, memory_address_register_1_s0, memory_address_register_1_s1,
       memory_address_register_1_s2, memory_address_register_1_s3, NCE, NEi, NLa, NLb, NLi, NLm, NLo, Op0,
       Op1, Op2, ram_1_s0, ram_1_s1, ram_1_s2, ram_1_s3, ram_1_s4, ram_1_s5, ram_1_s6, ram_1_s7,
       register_b_1_s0, register_b_1_s1, register_b_1_s2, register_b_1_s3, register_b_1_s4, register_b_1_s5,
       register_b_1_s6, register_b_1_s7, ula_1_eq, ula_1_out_20, ula_1_plus;
  wire [3:0] register_out_1_s0, register_out_1_s4;

  RAM ram_1 (
    .I0(I0), .I1(I1), .I2(I2), .I3(I3), .I4(I4), .I5(I5), .I6(I6), .I7(I7), .NCe(NCE), .Clr(Clr), .Clk(Clk),
    .A(memory_address_register_1_s0), .B(memory_address_register_1_s1), .C(memory_address_register_1_s2),
    .Ad(memory_address_register_1_s3), .S0(ram_1_s0), .S1(ram_1_s1), .S2(ram_1_s2), .S3(ram_1_s3),
    .S4(ram_1_s4), .S5(ram_1_s5), .S6(ram_1_s6), .S7(ram_1_s7));
  Instruction_Register instruction_register_1 (
    .NEi(NEi), .Clr(Clr), .Clk(Clk), .NLi(NLi), .I0(ram_1_s0), .I1(ram_1_s1), .I2(ram_1_s2), .I3(ram_1_s3),
    .I4(ram_1_s4), .I5(ram_1_s5), .I6(ram_1_s6), .I7(ram_1_s7), .C0(instruction_register_1_c0),
    .C1(instruction_register_1_c1), .C2(instruction_register_1_c2), .C3(instruction_register_1_c3),
    .Op0(ram_1_s4), .Op1(ram_1_s5), .Op2(ram_1_s6), .Op3(ram_1_s7));
  Button u_Clk (.out(Clk));
  Button u_Clr (.out(Clr));
  Program_Counter program_counter_1 (
    .Cp(Cp), .Ep(Ep), .Clr(Clr), .NClk(Clk), .S0(ram_1_s0), .S1(ram_1_s1), .S2(ram_1_s2), .S3(ram_1_s3));
  Controller controller_1 (
    .Clk(Clk), .Ori(Clr), .I0(instruction_register_1_c0), .I1(instruction_register_1_c1),
    .I2(instruction_register_1_c2), .I3(instruction_register_1_c3), .Ep(Ep), .Cp(Cp), .NLm(NLm), .NEi(NEi),
    .WRAM(NCE), .NLi(NLi), .Ea(Ea), .NLa(NLa), .Op0(Op0), .Op1(Op1), .Op2(Op2), .Eu(Eu), .NLb(NLb),
    .NLo(NLo), .HLT(controller_1_hlt));  // open: WRITE, READ, RRAM, L1, L2, L3, L4, L5, L6
  Memory_Address_Register memory_address_register_1 (
    .NLm(NLm), .Clk(Clk), .I0(ram_1_s0), .I1(ram_1_s1), .I2(ram_1_s2), .I3(ram_1_s3),
    .S0(memory_address_register_1_s0), .S1(memory_address_register_1_s1), .S2(memory_address_register_1_s2),
    .S3(memory_address_register_1_s3));  // open: S4, S5, S6, S7
  Register_B register_b_1 (
    .NLb(NLb), .Clk(Clk), .I0(ram_1_s0), .I1(ram_1_s1), .I2(ram_1_s2), .I3(ram_1_s3), .I4(ram_1_s4),
    .I5(ram_1_s5), .I6(ram_1_s6), .I7(ram_1_s7), .S0(register_b_1_s0), .S1(register_b_1_s1),
    .S2(register_b_1_s2), .S3(register_b_1_s3), .S4(register_b_1_s4), .S5(register_b_1_s5),
    .S6(register_b_1_s6), .S7(register_b_1_s7));
  Register_OUT register_out_1 (
    .NLo(NLo), .Clk(Clk), .I0(ram_1_s0), .I1(ram_1_s1), .I2(ram_1_s2), .I3(ram_1_s3), .I4(ram_1_s4),
    .I5(ram_1_s5), .I6(ram_1_s6), .I7(ram_1_s7), .S0(register_out_1_s0[0]), .S1(register_out_1_s0[1]),
    .S2(register_out_1_s0[2]), .S3(register_out_1_s0[3]), .S4(register_out_1_s4[0]),
    .S5(register_out_1_s4[1]), .S6(register_out_1_s4[2]), .S7(register_out_1_s4[3]));
  Acumulator acumulator_1 (
    .NLa(NLa), .Ea(Ea), .Clk(Clk), .I0(ram_1_s0), .I1(ram_1_s1), .I2(ram_1_s2), .I3(ram_1_s3), .I4(ram_1_s4),
    .I5(ram_1_s5), .I6(ram_1_s6), .I7(ram_1_s7), .S0(acumulator_1_s0), .S1(acumulator_1_s1),
    .S2(acumulator_1_s2), .S3(acumulator_1_s3), .S4(acumulator_1_s4), .S5(acumulator_1_s5),
    .S6(acumulator_1_s6), .S7(acumulator_1_s7));
  ULA ula_1 (
    .A0(acumulator_1_s0), .B0(register_b_1_s0), .A1(acumulator_1_s1), .B1(register_b_1_s1),
    .A2(acumulator_1_s2), .B2(register_b_1_s2), .A3(acumulator_1_s3), .B3(register_b_1_s3),
    .A4(acumulator_1_s4), .B4(register_b_1_s4), .A5(acumulator_1_s5), .B5(register_b_1_s5),
    .A6(acumulator_1_s6), .B6(register_b_1_s6), .A7(acumulator_1_s7), .B7(register_b_1_s7), .C0(Op0),
    .C1(Op1), .C2(Op2), .Eu(Eu), .out_20(ula_1_out_20), .eq(ula_1_eq), .plus(ula_1_plus), .S0(ram_1_s0),
    .S1(ram_1_s1), .S2(ram_1_s2), .S3(ram_1_s3), .S4(ram_1_s4), .S5(ram_1_s5), .S6(ram_1_s6), .S7(ram_1_s7));
  Seven_Seg_Hex seven_seg_hex_1 (.d(register_out_1_s4), .dp(1'b0));
  Seven_Seg_Hex seven_seg_hex_2 (.d(register_out_1_s0), .dp(1'b0));
  LED plus (.in(ula_1_plus));
  LED led (.in(ula_1_out_20));
  LED eq (.in(ula_1_eq));
  LED HLT (.in(controller_1_hlt));

  // Notes on the sheet:
  //   000 - Sum
  //   001 - Sub
  //   010 - Comp
  //   011 - Multi
  //   100 - ShiftR
  //   101 - ShiftL
  //   EXECUTE:
  //   T3:
  //   FETCH:
  //   T0, T1, T2
endmodule
