// Digital circuit Memory Address Register.dig as structural Verilog
module Memory_Address_Register (
  input  NLm,
  input  Clk,
  input  I0,
  input  I1,
  input  I2,
  output S0,
  output S1,
  output S2
);

  wire not_1_out, register_1_q3;

  not not_1 (not_1_out, NLm);
  Register register_1 (
    .Clk(Clk), .R(1'b1), .D0(I0), .W(not_1_out), .Clr(I1), .D1(I2), .Q0(S0), .Q1(S1), .Q2(S2),
    .Q3(register_1_q3), .Q4(register_1_q3), .Q5(register_1_q3), .Q6(register_1_q3), .Q7(register_1_q3));  // open: D2, D3, D4, D5, D6, D7
  // also tied to GND on the sheet: register_1_q3
endmodule
