// Digital circuit Register.dig as structural Verilog
module Register (
  input  Clk,
  input  Read,
  input  D0,
  input  Write,
  input  Clr,
  input  D1,
  input  D2,
  input  D3,
  input  D4,
  input  D5,
  input  D6,
  input  D7,
  output Q0,
  output Q1,
  output Q2,
  output Q3,
  output Q4,
  output Q5,
  output Q6,
  output Q7
);

  wire and_1_out, and_2_out, and_3_out, and_4_out, and_5_out, and_6_out, and_7_out, and_8_out, and_9_out,
       d_ff_1_q, d_ff_2_q, d_ff_3_q, d_ff_4_q, d_ff_5_q, d_ff_6_q, d_ff_7_q, d_ff_8_q, driver_1_out,
       driver_2_out, driver_3_out, driver_4_out, driver_5_out, driver_6_out, driver_7_out, driver_8_out;

  and and_1 (and_1_out, Write, ~Clr);  // And
  and and_2 (and_2_out, D7, and_1_out);
  D_FF d_ff_1 (.D(and_2_out), .C(Clk), .Q(d_ff_1_q));  // open: nQ
  assign driver_1_out = Read ? d_ff_1_q : 1'bz;  // Driver driver_1
  PullDown pulldown_1 (.out(Q7));
  DiodeForward diodeforward_1 (.in(driver_1_out), .out(Q7));
  and and_3 (and_3_out, D6, and_1_out);
  D_FF d_ff_2 (.D(and_3_out), .C(Clk), .Q(d_ff_2_q));  // open: nQ
  assign driver_2_out = Read ? d_ff_2_q : 1'bz;  // Driver driver_2
  PullDown pulldown_2 (.out(Q6));
  DiodeForward diodeforward_2 (.in(driver_2_out), .out(Q6));
  and and_4 (and_4_out, D5, and_1_out);
  D_FF d_ff_3 (.D(and_4_out), .C(Clk), .Q(d_ff_3_q));  // open: nQ
  DiodeForward diodeforward_3 (.in(driver_3_out), .out(Q5));
  assign driver_3_out = Read ? d_ff_3_q : 1'bz;  // Driver driver_3
  PullDown pulldown_3 (.out(Q5));
  and and_5 (and_5_out, D4, and_1_out);
  D_FF d_ff_4 (.D(and_5_out), .C(Clk), .Q(d_ff_4_q));  // open: nQ
  PullDown pulldown_4 (.out(Q4));
  DiodeForward diodeforward_4 (.in(driver_4_out), .out(Q4));
  assign driver_4_out = Read ? d_ff_4_q : 1'bz;  // Driver driver_4
  and and_6 (and_6_out, D3, and_1_out);
  D_FF d_ff_5 (.D(and_6_out), .C(Clk), .Q(d_ff_5_q));  // open: nQ
  assign driver_5_out = Read ? d_ff_5_q : 1'bz;  // Driver driver_5
  PullDown pulldown_5 (.out(Q3));
  DiodeForward diodeforward_5 (.in(driver_5_out), .out(Q3));
  and and_7 (and_7_out, D2, and_1_out);
  D_FF d_ff_6 (.D(and_7_out), .C(Clk), .Q(d_ff_6_q));  // open: nQ
  assign driver_6_out = Read ? d_ff_6_q : 1'bz;  // Driver driver_6
  PullDown pulldown_6 (.out(Q2));
  DiodeForward diodeforward_6 (.in(driver_6_out), .out(Q2));
  and and_8 (and_8_out, D1, and_1_out);
  D_FF d_ff_7 (.D(and_8_out), .C(Clk), .Q(d_ff_7_q));  // open: nQ
  DiodeForward diodeforward_7 (.in(driver_7_out), .out(Q1));
  assign driver_7_out = Read ? d_ff_7_q : 1'bz;  // Driver driver_7
  PullDown pulldown_7 (.out(Q1));
  and and_9 (and_9_out, D0, and_1_out);
  D_FF d_ff_8 (.D(and_9_out), .C(Clk), .Q(d_ff_8_q));  // open: nQ
  PullDown pulldown_8 (.out(Q0));
  DiodeForward diodeforward_8 (.in(driver_8_out), .out(Q0));
  assign driver_8_out = Read ? d_ff_8_q : 1'bz;  // Driver driver_8
endmodule
